# Fritzing sketch Smart Irrigation IOT (saved by Fritzing 0.8.7b)
circuit board: 8.46667cm x 5.64444cm
breadboards: 1

parts:
  Raspberry_Pi_Zero1 = Raspberry Pi Zero
  YL-83_-_Control_Board1 = YL-83 Rain Sensor - Control Board
  YL-83_-_Detection_Board1 = YL-83 Rain Sensor - Detection Board
  DHT11_1 = DHT11 module
  KY-1 = Keyes Relay [package=THT]
  LED1 = LED - 5mm [color="Red (633nm)" package="5 mm [THT]"]
  LED2 = LEDs [package=led10mm]
  Part1 = FC-28 Soil Hygrometer Module - Probe
  Part2 = FC-28 Soil Hygrometer Module

nets:
  GND: Raspberry_Pi_Zero1.GND, YL-83_-_Control_Board1.GND, DHT11_1.GND, KY-1.ground, LED1.anode, LED2.C, Part2.GND
  N1: Raspberry_Pi_Zero1.GIPO8, DHT11_1.DATA
  N2: Raspberry_Pi_Zero1.GIPO24, Part2.DO
  N3: Raspberry_Pi_Zero1.GIPO23, YL-83_-_Control_Board1.DO
  N4: Raspberry_Pi_Zero1.GIPO18, KY-1.signal
  N5: Raspberry_Pi_Zero1.GIPO15, LED2.A
  N6: Raspberry_Pi_Zero1.GIPO14, LED1.cathode
  VCC: Raspberry_Pi_Zero1.5V, YL-83_-_Control_Board1.VCC, DHT11_1.VCC, KY-1.power, Part2.VCC
  N7: YL-83_-_Control_Board1.POS, Part1.POS
  N8: YL-83_-_Control_Board1.NEG, Part1.NEG
  N9: YL-83_-_Detection_Board1.POS, Part2.POS
  N10: YL-83_-_Detection_Board1.NEG, Part2.NEG

custom parts:
  YL-83 Rain Sensor - Control Board: The YL-83 is a rain sensor that has more resistance when dry and less resistance when wet. The module runs at 5V.
  YL-83 Rain Sensor - Detection Board: The YL-83 is a rain sensor that has more resistance when dry and less resistance when wet. The module runs at 5V.
  DHT11 module: DHT11 black pcb module
  Keyes Relay: The Keyes 5V relay module is suitable for SCM development, home appliance control. It uses a 5V~12V TIL control signal which can control DC / AC signal.
  FC-28 Soil Hygrometer Module - Probe: The FC-28 is a soil hygrometer module that uses the Texas Instruments LM393 comparator chip to provide an analog measurement of soil humidity.
  FC-28 Soil Hygrometer Module: The FC-28 is a soil hygrometer module that uses the Texas Instruments LM393 comparator chip to provide an analog measurement of soil humidity. The digital output is high when soil moisture is over a certain threshold, as determined by adjusting the potentiometer.
